# Fritzing sketch Schematic (saved by Fritzing 0.9.6b)
breadboards: 2

parts:
  Mod1 = Heltec WiFi Kit 8 [part_number=HTIT-W8266]
  IC1 = MCP23017 I2C I/O Expander
  R1 = Resistor [tolerance=±5% resistance=10k package="1206 [SMD]"]
  LED1 = RGB LED (com. anode, rbg) [package="5 mm [THT]"]
  LED2 = RGB LED (com. anode, rbg) [package="5 mm [THT]"]
  Q1 = NPN-Transistor [package="TO92 [THT]"]
  Q2 = NPN-Transistor [package="TO92 [THT]"]
  Q3 = NPN-Transistor [package="TO92 [THT]"]
  Q4 = NPN-Transistor [package="TO92 [THT]"]
  Q5 = NPN-Transistor [package="TO92 [THT]"]
  Q6 = NPN-Transistor [package="TO92 [THT]"]
  R2 = Resistor [tolerance=±5% resistance=220 package="1206 [SMD]"]
  R3 = Resistor [tolerance=±5% resistance=220 package="1206 [SMD]"]
  RE4 = KY-040 Rotary encoder [package=THT]
  RE5 = KY-040 Rotary encoder [package=THT]
  RE6 = KY-040 Rotary encoder [package=THT]
  LED3 = smd LED [color="Green (570nm)" package="0805 [SMD]"]
  LED4 = smd LED [color="Red (633nm)" package="0805 [SMD]"]
  R4 = Resistor [tolerance=±5% resistance=330 package="1206 [SMD]"]
  R5 = Resistor [tolerance=±5% resistance=330 package="1206 [SMD]"]
  R6 = Resistor [tolerance=±5% resistance=220k package="1206 [SMD]"]
  R7 = Resistor [tolerance=±5% resistance=220k package="1206 [SMD]"]
  R8 = Resistor [tolerance=±5% resistance=220k package="1206 [SMD]"]
  R9 = Resistor [tolerance=±5% resistance=220k package="1206 [SMD]"]
  R10 = Resistor [tolerance=±5% resistance=220k package="1206 [SMD]"]
  R11 = Resistor [tolerance=±5% resistance=220k package="1206 [SMD]"]
  LED5 = smd LED [color="Infrared (940nm)" package="0805 [SMD]"]
  R12 = Resistor [tolerance=±5% resistance=330 package="1206 [SMD]"]
  IC2 = Dual Op-Amp [package=dip08]
  R13 = Resistor [tolerance=±5% resistance=56k package="2512 [SMD]"]
  R14 = Resistor [tolerance=±5% resistance=47k package="2512 [SMD]"]

nets:
  N1: Mod1.pin_2, IC1.SCL
  GND: Mod1.pin_9, Mod1.pin_12, Mod1.pin_13, Mod1.pin_16, IC1.VSS, IC1.A0, IC1.A1, IC1.A2, Q1.B, Q2.B, Q3.B, Q4.B, Q5.B, Q6.B, RE4.GND, RE5.GND, RE6.GND, R4.Pin_0, R5.Pin_0, LED5.cathode, IC2.A_V-, R14.Pin_0
  VCC: Mod1.pin_10, Mod1.pin_15, IC1.VDD, R1.Pin_1, LED1.blue_cathode, LED2.blue_cathode, RE5.Vcc, RE6.Vcc, IC2.A_V+, R13.Pin_0
  N2: Mod1.pin_11, Mod1.pin_14
  N3: Mod1.pin_17, IC1.SDA
  N4: Mod1.pin_18, R6.Pin_0
  N5: Mod1.pin_19, R12.Pin_1
  N6: Mod1.pin_20, R7.Pin_1
  N7: Mod1.pin_21, R8.Pin_1
  N8: Mod1.pin_22, R9.Pin_0
  N9: Mod1.pin_23, IC1.INTB
  N10: Mod1.pin_24, IC1.INTA
  N11: IC1.GPB0, LED4.anode
  N12: IC1.GPB1, LED3.anode
  N13: IC1.RESET, R1.Pin_0
  N14: IC1.GPA0, RE6.DT
  N15: IC1.GPA1, RE6.CLK
  N16: IC1.GPA2, RE5.DT
  N17: IC1.GPA4, RE4.DT
  N18: IC1.GPA5, RE4.CLK
  N19: LED1.red_cathode, R2.Pin_1
  N20: LED1.common_anode, Q2.E
  N21: LED1.green_cathode, Q3.E
  N22: LED2.red_cathode, R3.Pin_1
  N23: LED2.common_anode, Q5.E
  N24: LED2.green_cathode, Q6.E
  N25: Q1.E, R2.Pin_0
  N26: Q1.C, R6.Pin_1
  N27: Q2.C, R7.Pin_0
  N28: Q3.C, R8.Pin_0
  N29: Q4.E, R3.Pin_0
  N30: Q4.C, R9.Pin_1
  N31: Q5.C, R11.Pin_0
  N32: Q6.C, R10.Pin_0
  N33: LED3.cathode, R4.Pin_1
  N34: LED4.cathode, R5.Pin_1
  N35: R10.Pin_1, IC2.A_OUT
  N36: IC2.A_-IN, R13.Pin_1, R14.Pin_1

custom parts:
  Heltec WiFi Kit 8: The Heltec WiFi Kit 8 is an IoT development board designed and produced by Heltec Automation and based on the Espressif ESP8266 processor module. The board includes built-in WiFi, a 0.91″ OLED display and a Li-Po battery management system. Links: Heltec WiFi Kit 8 product page Github
  MCP23017 I2C I/O Expander: The MCP23017 uses two i2c pins (these can be shared with other i2c devices), and in exchange gives you 16 general purpose pins. You can set each of 16 pins to be input, output, input with a pullup or open drain. There's even the ability to get an interrupt via an external pin when any of the inputs change so you don't have to keep polling the chip.
  KY-040 Rotary encoder: KY-040 Rotary Encoder with switch on breakout borad from AZ Delivery
